# Fritzing sketch Fritzing pirsegmentmarcus (saved by Fritzing 0.9.3b)
breadboards: 1

parts:
  R1 = Resistor [tolerance=±5% resistance=220 package=THT]
  Part1 = Arduino Uno (Rev3)
  DI1 = 7-Segment LED Display [package=THT]
  R2 = Resistor [tolerance=±5% resistance=220 package="2010 [SMD]"]
  U1 = MLX90614 [package=to-39]  # not connected

nets:
  N1: R1.Pin_0, Part1.5V
  N2: R1.Pin_1, DI1.commAnode#7
  N3: Part1.D8, DI1.cathodeG
  N4: Part1.D9_PWM, DI1.cathodeF
  N5: Part1.D10_PWM/SS, DI1.cathodeE
  N6: Part1.D11_PWM/MOSI, DI1.cathodeD
  N7: Part1.D5_PWM, DI1.cathodeDP
  N8: Part1.D6_PWM, DI1.cathodeB
  N9: Part1.D7, DI1.cathodeA
  N10: Part1.GND, R2.Pin_1
  N11: DI1.commAnode#2, R2.Pin_0
